# Fritzing sketch BrewControllerV1.0 (saved by Fritzing 0.7.12b)
breadboards: 1

parts:
  Pi1 = Adafruit Pi Cobbler
  RaspberryPi1 = Raspberry Pi Model B
  R2 = Resistor [tolerance=±5% resistance=10k package=THT]
  Q1 = NPN-Transistor [package="TO92 [THT]"]
  Q2 = NPN-Transistor [package="TO92 [THT]"]
  LED1 = LED - 5mm [color="Red (633nm)" package="5 mm [THT]"]
  LED2 = LED - 5mm [color="Red (633nm)" package="5 mm [THT]"]
  R3 = Resistor [tolerance=±5% resistance=4.7k package=THT]
  R4 = Resistor [tolerance=±5% resistance=10k package=THT]
  DS1 = DS18B20 1-Wire Temperature Sensor Probe Cable
  S1 = Square Pushbutton
  S2 = Square Pushbutton
  DS2 = DS18B20 1-Wire Temperature Sensor Probe Cable

nets:
  3V3: Pi1.3V3, RaspberryPi1.3V3, R3.Pin_0, DS1.VDD, DS2.VDD
  GND: Pi1.GND, RaspberryPi1.GND, DS1.GND, DS2.GND
  N1: Pi1.#4, RaspberryPi1.#4, R3.Pin_1, DS1.DQ, DS2.DQ
  N2: Pi1.CE0, RaspberryPi1.CS0, R4.Pin_1
  N3: Pi1.CE1, RaspberryPi1.CS1, R2.Pin_1
  N4: R2.Pin_0, Q1.B, LED1.cathode, LED1.anode
  N5: Q1.E, S1.leg0
  N6: Q1.C, S1.leg1
  N7: Q2.E, S2.leg0
  N8: Q2.B, LED2.cathode, LED2.anode, R4.Pin_0
  N9: Q2.C, S2.leg1

custom parts:
  Adafruit Pi Cobbler: Adafruit Pi Cobbler GPIO Breakout for Raspberry Pi
  Raspberry Pi Model B: Raspberry Pi (Model B)
